# Fritzing sketch ESP8266_회로도 (saved by Fritzing 0.9.3b)

parts:
  U1 = NodeMCU V1.0
  부품2 = RFID-RC522-v3
  J1 = Piezo Speaker

nets:
  N1: U1.D1, J1.pin2
  N2: U1.D2, U1.D3, 부품2.RST
  3V3: U1.3V3, 부품2.3.3V
  GND: U1.GND, 부품2.GND, J1.pin1
  N3: U1.D5, 부품2.SCK
  N4: U1.D6, 부품2.MISO
  N5: U1.D7, 부품2.MOSI
  N6: U1.D8, U1.RX, 부품2.SDA

custom parts:
  NodeMCU V1.0: ESP8266 based NodeMCU
  RFID-RC522-v3: A simple China made RFID-RC522 Reader (6x4 cm); do check the pin labels, as this is a MFRC522 based clone.
